// Logisim project judge.circ as structural Verilog: 1 circuit, main circuit Win-Lose-Draw
module Win_Lose_Draw (
  input  [3:0] Tens,
  input  [3:0] Units,
  input  Is_Zero,
  input  Another,
  output out_5,
  output out_6
);

  wire comparator_1_eq, comparator_1_gt, xor_1_out;
  wire [7:0] adder_1_out, bit_extender_1_out, bit_extender_2_out, multiplier_1_out, register_1_q;

  assign bit_extender_1_out = {{4{1'b0}}, Tens};  // Bit_Extender bit_extender_1
  assign bit_extender_2_out = {{4{1'b0}}, Units};  // Bit_Extender bit_extender_2
  xor xor_1 (xor_1_out, Is_Zero, Another);
  Multiplier multiplier_1 (.a(8'ha), .b(bit_extender_1_out), .out(multiplier_1_out));  // open: cin, cout
  Adder adder_1 (.a(multiplier_1_out), .b(bit_extender_2_out), .out(adder_1_out));  // open: cin, cout
  Register register_1 (.D(adder_1_out), .Q(register_1_q), .clk(xor_1_out));  // open: en, clr
  Comparator comparator_1 (.a(register_1_q), .b(8'h18), .gt(comparator_1_gt), .eq(comparator_1_eq));  // open: lt
  or or_1 (out_5, comparator_1_gt, comparator_1_eq);
  or or_2 (out_6, register_1_q[0], register_1_q[1], register_1_q[2], register_1_q[3], register_1_q[4], register_1_q[5], register_1_q[6], register_1_q[7]);
endmodule
