// Logisim project utility.circ as structural Verilog: 7 circuits, main circuit Increment (4 bits)
module Gamepad_Address_Manager (
  input  [7:0] Input_Address,
  input  Data,
  output [3:0] Gamepad_Address,
  output Is_Selected
);

  wire comparator_1_lt, not_1_out;
  wire [3:0] bit_extender_1_out;

  Comparator #(.mode("unsigned")) comparator_1 (.a(8'hf0), .b(Input_Address), .lt(comparator_1_lt));  // open: gt, eq
  Bit_Extender #(.out_width(4)) bit_extender_1 (.in(Input_Address), .out(bit_extender_1_out));
  and and_1 (Is_Selected, comparator_1_lt, Data);
  assign Gamepad_Address = Is_Selected ? bit_extender_1_out : 4'bz;  // Controlled_Buffer controlled_buffer_1
  not not_1 (not_1_out, Is_Selected);
  assign Gamepad_Address = not_1_out ? 4'b0000 : 4'bz;  // Controlled_Buffer controlled_buffer_2
endmodule

module RAM_Address_Manager (
  input  [7:0] Input_Address,
  input  Data,
  output [3:0] RAM_Address,
  output Is_Selected
);

  wire and_1_out, comparator_1_lt, comparator_2_gt;
  wire [3:0] bit_extender_1_out;

  Comparator #(.mode("unsigned")) comparator_1 (.a(Input_Address), .b(8'hf0), .lt(comparator_1_lt));  // open: gt, eq
  Comparator #(.mode("unsigned")) comparator_2 (.a(Input_Address), .b(8'hdf), .gt(comparator_2_gt));  // open: eq, lt
  Bit_Extender #(.out_width(4)) bit_extender_1 (.in(Input_Address), .out(bit_extender_1_out));
  and and_1 (and_1_out, comparator_1_lt, comparator_2_gt);
  assign RAM_Address = Is_Selected ? bit_extender_1_out : 4'bz;  // Controlled_Buffer controlled_buffer_1
  and and_2 (Is_Selected, and_1_out, Data);
endmodule

module Memory_Manager (
  input  Address
);
endmodule

module Increment__4_bits (
  input  [3:0] in_1,
  output [3:0] out_2
);

  Adder #(.width(4)) adder_1 (.a(in_1), .b(4'b0001), .out(out_2));  // open: cin, cout
endmodule

module Is_Equal__4_bits (
  input  [3:0] A,
  input  [3:0] B,
  output R
);

  Comparator #(.width(4)) comparator_1 (.a(A), .b(B), .eq(R));  // open: gt, lt
endmodule

module Is_Equal__8_bits (
  input  [7:0] A,
  input  [7:0] B,
  output R
);

  Comparator comparator_1 (.a(A), .b(B), .eq(R));  // open: gt, lt
endmodule

module Not_Zero__6_bits (
  input  [5:0] in_1,
  output out_2
);

  wire or_1_out;

  or or_1 (or_1_out, in_1[0], in_1[1], in_1[2], in_1[3], in_1[4], in_1[5]);
  Transistor #(.\type ("n")) transistor_1 (.in(1'b0), .out(out_2), .gate(or_1_out));
endmodule
